// Logisim project Question1b.circ as structural Verilog: 1 circuit, main circuit main
// Potomkin Lev (8267361)
module main (
  input  A,
  input  B,
  input  C,
  output L
);

  wire or_1_out;

  or or_1 (or_1_out, A, B);
  or or_2 (L, or_1_out, C);
endmodule
