// Logisim project Question1d.circ as structural Verilog: 1 circuit, main circuit main
// Potomkin Lev (8267361)
module main (
  input  A,
  input  B,
  input  C,
  output W
);

  wire not_1_out, not_2_out;

  not not_1 (not_1_out, A);
  not not_2 (not_2_out, B);
  and and_1 (W, not_1_out, not_2_out);
endmodule
