// Logisim project Question2a.circ as structural Verilog: 1 circuit, main circuit main
// Potomkin Lev (8267361)
module main (
  input  A,
  input  B,
  input  C,
  output Y
);

  wire and_1_out, not_1_out;

  not not_1 (not_1_out, C);
  and and_1 (and_1_out, A, B);
  xor xor_1 (Y, and_1_out, not_1_out);
endmodule
