// Logisim project Question2c.circ as structural Verilog: 1 circuit, main circuit main
module main (
  input  A,
  input  C,
  input  B,
  output Y
);

  wire and_1_out, nand_1_out;

  nand nand_1 (nand_1_out, A, C);
  and and_1 (and_1_out, C, B);
  or or_1 (Y, nand_1_out, and_1_out);
endmodule
