// Logisim project Question3c.circ as structural Verilog: 1 circuit, main circuit main
// Potomkin Lev (8267361)
module main (
  input  F,
  input  L,
  input  R,
  input  B,
  output Mf,
  output Ml,
  output Mr,
  output Mb,
  output V
);

  wire and_1_out, and_4_out, not_1_out, not_2_out, not_3_out, not_4_out;

  not not_1 (not_1_out, F);
  not not_2 (not_2_out, L);
  not not_3 (not_3_out, R);
  not not_4 (not_4_out, B);
  and and_1 (and_1_out, not_1_out, not_2_out);
  and and_2 (Ml, not_1_out, L);
  and and_3 (Mr, and_1_out, R);
  and and_4 (and_4_out, and_1_out, not_3_out);
  and and_5 (Mb, and_4_out, B);
  and and_6 (V, and_4_out, not_4_out);

  assign Mf = F;
endmodule
