// Logisim project assignment3.circ as structural Verilog: 1 circuit, main circuit main
// Potomkin Lev (8267361)
module main (
  input  A5,
  input  A4,
  input  A3,
  input  A2,
  input  A1,
  input  A0,
  output CS_RAM,
  output CS_ROM,
  output CS_LCD,
  output CS_COM,
  output CS_LED
);

  wire and_2_out, and_4_out, and_5_out, and_6_out, not_2_out, not_3_out, not_4_out, not_5_out, not_6_out;

  not not_1 (CS_RAM, A5);
  not not_2 (not_2_out, A4);
  not not_3 (not_3_out, A3);
  not not_4 (not_4_out, A2);
  not not_5 (not_5_out, A1);
  not not_6 (not_6_out, A0);
  and and_1 (CS_ROM, A5, not_2_out);
  and and_2 (and_2_out, A5, A4);
  and and_3 (CS_LCD, and_2_out, A3);
  and and_4 (and_4_out, not_3_out, not_4_out);
  and and_5 (and_5_out, and_2_out, and_4_out);
  and and_6 (and_6_out, and_5_out, not_5_out);
  and and_7 (CS_COM, and_5_out, A1);
  and and_8 (CS_LED, and_6_out, not_6_out);
endmodule
